// Logisim project 8_bit_CPU.circ as structural Verilog: 9 circuits, main circuit main_cpu_schema
module main_cpu_schema (
  input  external_reset
);

  wire acall, alu_selB, b, clk, clock_1_out, control_unit_1_halt, d_ff_1_qn, dec_sp, inc_sp, internal_reset,
       mem_r, mem_w, rcall, reg_w_en, reset, ret, stack_ra_op, stall;
  wire [1:0] b_cond, mem_addr_sel, pc_wsel, reg_wsel;
  wire [2:0] rd, rs1, rs2;
  wire [3:0] alu_op, flags;
  wire [4:0] imm5;
  wire [7:0] alu_result, imm8, mem_address_calculator_1_eff_addr, mem_rdata, multiplexer_2_out,
       multiplexer_3_out, regA, regB, sp;
  wire [10:0] imm11, pc, ra;
  wire [15:0] instruction_register_q, multiplexer_1_out, rom_1_data;

  ROM #(.addrWidth(11), .dataWidth(16)) rom_1 (.addr(pc), .data(rom_1_data));
  Clock clock_1 (.out(clock_1_out));
  D_Flip_Flop d_ff_1 (.D(control_unit_1_halt), .clk(clk), .Qn(d_ff_1_qn));  // open: Q, preset, reset
  Register #(.width(16)) instruction_register (
    .D(multiplexer_1_out), .clk(clk), .Q(instruction_register_q), .clr(reset));  // open: en
  Multiplexer #(.width(16)) multiplexer_1 (.in0(rom_1_data), .in1({16{1'b0}}), .out(multiplexer_1_out), .sel(stall));
  and and_1 (clk, clock_1_out, d_ff_1_qn);
  control_unit control_unit_1 (
    .instruction(instruction_register_q), .alu_op(alu_op), .rd(rd), .rs1(rs1), .rs2(rs2), .imm5(imm5),
    .imm8(imm8), .imm11(imm11), .reg_w(reg_w_en), .reg_wsel(reg_wsel), .alu_selB(alu_selB), .mem_r(mem_r),
    .mem_w(mem_w), .mem_addr_sel(mem_addr_sel), .stall_pin(stall), .reset(internal_reset), .pc_wsel(pc_wsel),
    .b(b), .b_cond(b_cond), .rcall(rcall), .halt(control_unit_1_halt), .inc_sp(inc_sp), .dec_sp(dec_sp),
    .acall(acall), .ret(ret));  // open: nop
  or or_1 (reset, internal_reset, external_reset);
  Multiplexer #(.select(2), .width(8)) multiplexer_2 (
    .in0(alu_result), .in1(imm8), .in2(mem_rdata), .in3({8{1'b0}}), .out(multiplexer_2_out), .sel(reg_wsel));
  and and_2 (stack_ra_op, imm8[0], imm8[1], imm8[2], imm8[3], imm8[4], imm8[5], imm8[6], imm8[7]);
  // Probe on regA
  register_file register_file_1 (
    .write_data(multiplexer_2_out), .write_address(rd), .write_enable(reg_w_en), .read_address_A(rs1),
    .read_address_B(rs2), .clock(clk), .reset(reset), .read_data_A(regA), .read_data_B(regB));
  // Probe on regB
  // Probe on sp
  sp_unit sp_unit_1 (
    .dec_sp(dec_sp), .stack_ra_op(stack_ra_op), .inc_sp(inc_sp), .reset(reset), .clk(clk), .sp_addr(sp));
  Multiplexer #(.width(8)) multiplexer_3 (.in0(regB), .in1(imm8), .out(multiplexer_3_out), .sel(alu_selB));
  // Probe on alu_result
  alu alu_1 (.code(alu_op), .a(regA), .b(multiplexer_3_out), .clk(clk), .result(alu_result), .flags(flags));
  mem_address_calculator mem_address_calculator_1 (
    .mem_addr_sel(mem_addr_sel), .imm8(imm8), .base_reg(regA), .imm5(imm5), .sp(sp),
    .eff_addr(mem_address_calculator_1_eff_addr));
  RAM ram_1 (.addr(mem_address_calculator_1_eff_addr), .we(mem_w), .oe(mem_r), .clk(clk), .din(regA), .dout(mem_rdata));
  pc_unit pc_unit_1 (
    .w_sel(pc_wsel), .imm11(imm11), .ret_addr(ra), .b(b), .reset(reset), .flags(flags), .b_cond(b_cond),
    .rcall(rcall), .clk(clk), .pc_addr(pc));
  // Probe on pc
  ra_unit ra_unit_1 (.pc(pc), .ret(ret), .rcall(rcall), .acall(acall), .reset(reset), .clk(clk), .ra(ra));

  // Notes on the sheet:
  //   contents of rom_1 (hex, n*v repeats v):
  //   7911 b804 8910 c006 6922 e000 1624 a020 7fee 8f11 f100 7914 7a06 328 1368 6b05 7301 8b10 793c 7a0f
  //   2328 2b68 3364 3b60 8b11 7981 7c02 4230 5330 4c84 5b30 6370 8b11 7c20 7955 9983 9283 8515 7daa d500
  //   7d00 dd00 8d16
endmodule

module alu (
  input  [3:0] code,
  input  [7:0] a,
  input  [7:0] b,
  input  clk,
  output [7:0] result,
  output [3:0] flags
);

  wire adder_1_cout, adder_2_cout, d_ff_1_q, sub, subtractor_1_bout, subtractor_2_bout, xnor_1_out,
       xor_2_out, xor_3_out;
  wire [2:0] bitselector_1_out, xnor_2_out;
  wire [7:0] adder_1_out, adder_2_out, adder_3_out, and_1_out, not_1_out, or_1_out, shifter_1_out,
       shifter_2_out, shifter_3_out, shifter_4_out, shifter_5_out, subtractor_1_out, subtractor_2_out,
       subtractor_3_out, xor_1_out;

  D_Flip_Flop d_ff_1 (.D(flags[0]), .clk(clk), .Q(d_ff_1_q));  // open: Qn, preset, reset
  BitSelector #(.group(3)) bitselector_1 (.in(b), .out(bitselector_1_out), .sel(2'b00));
  Adder adder_1 (.a(a), .b(b), .out(adder_1_out), .cout(adder_1_cout));  // open: cin
  Adder adder_2 (.a(a), .b(b), .out(adder_2_out), .cin(d_ff_1_q), .cout(adder_2_cout));
  Subtractor subtractor_1 (.a(a), .b(b), .out(subtractor_1_out), .bout(subtractor_1_bout));  // open: bin
  Subtractor subtractor_2 (.a(a), .b(b), .out(subtractor_2_out), .bin(d_ff_1_q), .bout(subtractor_2_bout));
  assign and_1_out = a & b;  // AND_Gate and_1, 8 bits wide
  assign or_1_out = a | b;  // OR_Gate or_1, 8 bits wide
  assign xor_1_out = a ^ b;  // XOR_Gate xor_1, 8 bits wide
  assign not_1_out = ~a;  // NOT_Gate not_1, 8 bits wide
  Shifter shifter_1 (.in(a), .\dist (bitselector_1_out), .out(shifter_1_out));
  Shifter #(.shift("lr")) shifter_2 (.in(a), .\dist (bitselector_1_out), .out(shifter_2_out));
  Shifter #(.shift("ar")) shifter_3 (.in(a), .\dist (bitselector_1_out), .out(shifter_3_out));
  Shifter #(.shift("rl")) shifter_4 (.in(a), .\dist (bitselector_1_out), .out(shifter_4_out));
  Shifter #(.shift("rr")) shifter_5 (.in(a), .\dist (bitselector_1_out), .out(shifter_5_out));
  Adder adder_3 (.a(a), .b(b), .out(adder_3_out));  // open: cin, cout
  Subtractor subtractor_3 (.a(a), .b(b), .out(subtractor_3_out));  // open: bin, bout
  Multiplexer #(.select(4), .width(8)) multiplexer_1 (
    .in0(adder_1_out), .in1(adder_2_out), .in2(subtractor_1_out), .in3(subtractor_2_out), .in4(and_1_out),
    .in5(or_1_out), .in6(xor_1_out), .in7(not_1_out), .in8(shifter_1_out), .in9(shifter_2_out),
    .in10(shifter_3_out), .in11(shifter_4_out), .in12(shifter_5_out), .in13(adder_3_out),
    .in14(subtractor_3_out), .in15({8{1'b0}}), .out({flags[2], result[6:0]}), .sel(code));
  xor xor_2 (xor_2_out, b[7], sub);
  Multiplexer #(.select(4)) multiplexer_2 (
    .in0(adder_1_cout), .in1(adder_2_cout), .in2(subtractor_1_bout), .in3(subtractor_2_bout), .in4(d_ff_1_q),
    .in5(d_ff_1_q), .in6(d_ff_1_q), .in7(d_ff_1_q), .in8(d_ff_1_q), .in9(d_ff_1_q), .in10(d_ff_1_q),
    .in11(d_ff_1_q), .in12(d_ff_1_q), .in13(d_ff_1_q), .in14(d_ff_1_q), .in15(d_ff_1_q), .out(flags[0]),
    .sel(code));
  xor xor_3 (xor_3_out, flags[2], a[7]);
  xnor xnor_1 (xnor_1_out, a[7], xor_2_out);
  nor nor_1 (flags[1], result[0], result[1], result[2], result[3], result[4], result[5], result[6], flags[2]);
  and and_2 (flags[3], xor_3_out, xnor_1_out);
  assign xnor_2_out = ~(code[3:1] ^ 3'b001);  // XNOR_Gate xnor_2, 3 bits wide
  and and_3 (sub, xnor_2_out[0], xnor_2_out[1], xnor_2_out[2]);

  assign result[7] = flags[2];

  // Other names for the same wires on the sheet: a_msb = a[7]; b_msb = b[7]; carry = flags[0]; zero = flags[1];
  //   negative = flags[2]; overflow = flags[3]
endmodule

module register_file (
  input  [7:0] write_data,
  input  [2:0] write_address,
  input  write_enable,
  input  [2:0] read_address_A,
  input  [2:0] read_address_B,
  input  clock,
  input  reset,
  output [7:0] read_data_A,
  output [7:0] read_data_B
);

  wire and_1_out, and_2_out, and_3_out, and_4_out, and_5_out, and_6_out, and_7_out, decoder_1_out1,
       decoder_1_out2, decoder_1_out3, decoder_1_out4, decoder_1_out5, decoder_1_out6, decoder_1_out7;
  wire [7:0] register_1_q, register_2_q, register_3_q, register_4_q, register_5_q, register_6_q, register_7_q;

  Decoder #(.select(3)) decoder_1 (
    .out1(decoder_1_out1), .out2(decoder_1_out2), .out3(decoder_1_out3), .out4(decoder_1_out4),
    .out5(decoder_1_out5), .out6(decoder_1_out6), .out7(decoder_1_out7), .sel(write_address),
    .en(write_enable));  // open: out0
  and and_1 (and_1_out, decoder_1_out1, clock);
  and and_2 (and_2_out, decoder_1_out2, clock);
  and and_3 (and_3_out, decoder_1_out3, clock);
  and and_4 (and_4_out, decoder_1_out4, clock);
  and and_5 (and_5_out, decoder_1_out5, clock);
  and and_6 (and_6_out, decoder_1_out6, clock);
  and and_7 (and_7_out, decoder_1_out7, clock);
  Register register_1 (.D(write_data), .en(and_1_out), .clk(clock), .Q(register_1_q), .clr(reset));
  Register register_2 (.D(write_data), .en(and_2_out), .clk(clock), .Q(register_2_q), .clr(reset));
  Register register_3 (.D(write_data), .en(and_3_out), .clk(clock), .Q(register_3_q), .clr(reset));
  Register register_4 (.D(write_data), .en(and_4_out), .clk(clock), .Q(register_4_q), .clr(reset));
  Register register_5 (.D(write_data), .en(and_5_out), .clk(clock), .Q(register_5_q), .clr(reset));
  Register register_6 (.D(write_data), .en(and_6_out), .clk(clock), .Q(register_6_q), .clr(reset));
  Register register_7 (.D(write_data), .en(and_7_out), .clk(clock), .Q(register_7_q), .clr(reset));
  Multiplexer #(.select(3), .width(8)) multiplexer_1 (
    .in0({8{1'b0}}), .in1(register_1_q), .in2(register_2_q), .in3(register_3_q), .in4(register_4_q),
    .in5(register_5_q), .in6(register_6_q), .in7(register_7_q), .out(read_data_A), .sel(read_address_A));
  Multiplexer #(.select(3), .width(8)) multiplexer_2 (
    .in0({8{1'b0}}), .in1(register_1_q), .in2(register_2_q), .in3(register_3_q), .in4(register_4_q),
    .in5(register_5_q), .in6(register_6_q), .in7(register_7_q), .out(read_data_B), .sel(read_address_B));
endmodule

module control_unit (
  input  [15:0] instruction,
  output [3:0] alu_op,
  output [2:0] rd,
  output [2:0] rs1,
  output [2:0] rs2,
  output [4:0] imm5,
  output [7:0] imm8,
  output [10:0] imm11,
  output reg_w,
  output [1:0] reg_wsel,
  output alu_selB,
  output mem_r,
  output mem_w,
  output [1:0] mem_addr_sel,
  output stall_pin,
  output reset,
  output [1:0] pc_wsel,
  output b,
  output [1:0] b_cond,
  output rcall,
  output halt,
  output inc_sp,
  output dec_sp,
  output acall,
  output ret,
  output nop
);

  wire instruction_decoder_1_is_add, instruction_decoder_1_is_addc, instruction_decoder_1_is_addi,
       instruction_decoder_1_is_and, instruction_decoder_1_is_asr, instruction_decoder_1_is_brn,
       instruction_decoder_1_is_brv, instruction_decoder_1_is_brz, instruction_decoder_1_is_jmp,
       instruction_decoder_1_is_lda, instruction_decoder_1_is_lia, instruction_decoder_1_is_not,
       instruction_decoder_1_is_or, instruction_decoder_1_is_rol, instruction_decoder_1_is_ror,
       instruction_decoder_1_is_sda, instruction_decoder_1_is_shl, instruction_decoder_1_is_shr,
       instruction_decoder_1_is_sia, instruction_decoder_1_is_sub, instruction_decoder_1_is_subc,
       instruction_decoder_1_is_subi, instruction_decoder_1_is_xor;

  instruction_decoder instruction_decoder_1 (
    .opcode(instruction[15:11]), .is_add(instruction_decoder_1_is_add),
    .is_addc(instruction_decoder_1_is_addc), .is_sub(instruction_decoder_1_is_sub),
    .is_subc(instruction_decoder_1_is_subc), .is_and(instruction_decoder_1_is_and),
    .is_or(instruction_decoder_1_is_or), .is_xor(instruction_decoder_1_is_xor),
    .is_not(instruction_decoder_1_is_not), .is_shl(instruction_decoder_1_is_shl),
    .is_shr(instruction_decoder_1_is_shr), .is_asr(instruction_decoder_1_is_asr),
    .is_rol(instruction_decoder_1_is_rol), .is_ror(instruction_decoder_1_is_ror),
    .is_addi(instruction_decoder_1_is_addi), .is_subi(instruction_decoder_1_is_subi), .is_ldi(reg_wsel[0]),
    .is_lda(instruction_decoder_1_is_lda), .is_sda(instruction_decoder_1_is_sda),
    .is_lia(instruction_decoder_1_is_lia), .is_sia(instruction_decoder_1_is_sia),
    .is_brz(instruction_decoder_1_is_brz), .is_brn(instruction_decoder_1_is_brn),
    .is_brv(instruction_decoder_1_is_brv), .is_acall(acall), .is_jmp(instruction_decoder_1_is_jmp),
    .is_rcall(rcall), .is_push(dec_sp), .is_pop(inc_sp), .is_ret(ret), .is_nop(nop), .is_reset(reset),
    .is_halt(halt));
  or or_1 (reg_w, instruction_decoder_1_is_add, instruction_decoder_1_is_addc, instruction_decoder_1_is_sub, instruction_decoder_1_is_subc, instruction_decoder_1_is_and, instruction_decoder_1_is_or, instruction_decoder_1_is_xor, instruction_decoder_1_is_not, instruction_decoder_1_is_shl, instruction_decoder_1_is_shr, instruction_decoder_1_is_asr, instruction_decoder_1_is_rol, instruction_decoder_1_is_ror, instruction_decoder_1_is_addi, instruction_decoder_1_is_subi, reg_wsel[0], instruction_decoder_1_is_lda, instruction_decoder_1_is_lia, inc_sp);
  or or_2 (reg_wsel[1], instruction_decoder_1_is_lda, instruction_decoder_1_is_lia);
  or or_3 (alu_selB, instruction_decoder_1_is_addi, instruction_decoder_1_is_subi);
  or or_4 (mem_r, instruction_decoder_1_is_lda, instruction_decoder_1_is_lia, inc_sp);
  or or_5 (mem_w, instruction_decoder_1_is_sda, instruction_decoder_1_is_sia, dec_sp);
  or or_6 (mem_addr_sel[0], instruction_decoder_1_is_lia, instruction_decoder_1_is_sia);
  or or_7 (mem_addr_sel[1], dec_sp, inc_sp);
  or or_8 (stall_pin, instruction_decoder_1_is_brz, instruction_decoder_1_is_brn, acall, instruction_decoder_1_is_brv, instruction_decoder_1_is_jmp, rcall, ret);
  or or_9 (pc_wsel[0], instruction_decoder_1_is_brz, instruction_decoder_1_is_brn, instruction_decoder_1_is_brv, ret);
  or or_10 (pc_wsel[1], instruction_decoder_1_is_jmp, acall, ret);
  or or_11 (b, instruction_decoder_1_is_brz, instruction_decoder_1_is_brn, instruction_decoder_1_is_brv);
  or or_12 (b_cond[0], instruction_decoder_1_is_brz, instruction_decoder_1_is_brv);
  or or_13 (b_cond[1], instruction_decoder_1_is_brn, instruction_decoder_1_is_brv);

  assign alu_op = instruction[14:11];
  assign imm5 = instruction[4:0];
  assign imm8 = instruction[7:0];
  assign imm11 = instruction[10:0];
  assign rd = instruction[10:8];
  assign rs1 = instruction[7:5];
  assign rs2 = instruction[4:2];
endmodule

module instruction_decoder (
  input  [4:0] opcode,
  output is_add,
  output is_addc,
  output is_sub,
  output is_subc,
  output is_and,
  output is_or,
  output is_xor,
  output is_not,
  output is_shl,
  output is_shr,
  output is_asr,
  output is_rol,
  output is_ror,
  output is_addi,
  output is_subi,
  output is_ldi,
  output is_lda,
  output is_sda,
  output is_lia,
  output is_sia,
  output is_brz,
  output is_brn,
  output is_brv,
  output is_acall,
  output is_jmp,
  output is_rcall,
  output is_push,
  output is_pop,
  output is_ret,
  output is_nop,
  output is_reset,
  output is_halt
);

  Decoder #(.select(5)) decoder_1 (
    .out0(is_add), .out1(is_addc), .out2(is_sub), .out3(is_subc), .out4(is_and), .out5(is_or), .out6(is_xor),
    .out7(is_not), .out8(is_shl), .out9(is_shr), .out10(is_asr), .out11(is_rol), .out12(is_ror),
    .out13(is_addi), .out14(is_subi), .out15(is_ldi), .out16(is_lda), .out17(is_sda), .out18(is_lia),
    .out19(is_sia), .out20(is_brz), .out21(is_brn), .out22(is_brv), .out23(is_acall), .out24(is_jmp),
    .out25(is_rcall), .out26(is_push), .out27(is_pop), .out28(is_ret), .out29(is_nop), .out30(is_reset),
    .out31(is_halt), .sel(opcode));  // open: en
endmodule

module mem_address_calculator (
  input  [1:0] mem_addr_sel,
  input  [7:0] imm8,
  input  [7:0] base_reg,
  input  [4:0] imm5,
  input  [7:0] sp,
  output [7:0] eff_addr
);

  wire [7:0] adder_1_out, bit_extender_1_out;

  assign bit_extender_1_out = {{3{imm5[4]}}, imm5};  // Bit_Extender bit_extender_1
  Adder adder_1 (.a(base_reg), .b(bit_extender_1_out), .out(adder_1_out));  // open: cin, cout
  Multiplexer #(.select(2), .width(8)) multiplexer_1 (
    .in0(imm8), .in1(adder_1_out), .in2(sp), .in3({8{1'b0}}), .out(eff_addr), .sel(mem_addr_sel));
endmodule

module pc_unit (
  input  [1:0] w_sel,
  input  [10:0] imm11,
  input  [10:0] ret_addr,
  input  b,
  input  reset,
  input  [3:0] flags,
  input  [1:0] b_cond,
  input  rcall,
  input  clk,
  output [10:0] pc_addr
);

  wire and_1_out, bitselector_1_out, or_1_out;
  wire [3:0] register_1_q;
  wire [10:0] adder_1_out, adder_2_out, multiplexer_1_out, multiplexer_2_out;

  Register #(.width(4)) register_1 (.D(flags), .clk(clk), .Q(register_1_q));  // open: en, clr
  and and_1 (and_1_out, b, bitselector_1_out);
  BitSelector #(.width(4)) bitselector_1 (.in(register_1_q), .out(bitselector_1_out), .sel(b_cond));
  Multiplexer #(.width(11)) multiplexer_1 (.in0(11'h1), .in1(imm11), .out(multiplexer_1_out), .sel(or_1_out));
  or or_1 (or_1_out, and_1_out, rcall);
  Adder #(.width(11)) adder_1 (.a(11'h1), .b(pc_addr), .out(adder_1_out));  // open: cin, cout
  Adder #(.width(11)) adder_2 (.a(pc_addr), .b(multiplexer_1_out), .out(adder_2_out));  // open: cin, cout
  Register #(.width(11)) pc (.D(multiplexer_2_out), .clk(clk), .Q(pc_addr), .clr(reset));  // open: en
  Multiplexer #(.select(2), .width(11)) multiplexer_2 (
    .in0(adder_1_out), .in1(adder_2_out), .in2(imm11), .in3(ret_addr), .out(multiplexer_2_out), .sel(w_sel));
endmodule

module sp_unit (
  input  dec_sp,
  input  stack_ra_op,
  input  inc_sp,
  input  reset,
  input  clk,
  output [7:0] sp_addr
);

  wire and_1_out, and_2_out, or_1_out;
  wire [7:0] adder_1_out, multiplexer_1_out, subtractor_1_out;

  Adder adder_1 (.a(sp_addr), .b(8'h1), .out(adder_1_out));  // open: cin, cout
  Subtractor subtractor_1 (.a(sp_addr), .b(8'h1), .out(subtractor_1_out));  // open: bin, bout
  and and_1 (and_1_out, dec_sp, stack_ra_op);
  and and_2 (and_2_out, stack_ra_op, inc_sp);
  Multiplexer #(.width(8)) multiplexer_1 (
    .in0(adder_1_out), .in1(subtractor_1_out), .out(multiplexer_1_out), .sel(and_1_out));
  Register sp (.D(multiplexer_1_out), .en(or_1_out), .clk(clk), .Q(sp_addr), .clr(reset));
  or or_1 (or_1_out, and_1_out, and_2_out);
endmodule

module ra_unit (
  input  [10:0] pc,
  input  ret,
  input  rcall,
  input  acall,
  input  reset,
  input  clk,
  output [10:0] ra
);

  wire or_1_out;
  wire [7:0] adder_1_out, multiplexer_1_out, sp_q, subtractor_1_out;
  wire [10:0] adder_2_out, multiplexer_2_out, ram_1_dout;

  Subtractor subtractor_1 (.a(sp_q), .b(8'h1), .out(subtractor_1_out));  // open: bin, bout
  Adder adder_1 (.a(sp_q), .b(8'h1), .out(adder_1_out));  // open: cin, cout
  Adder #(.width(11)) adder_2 (.a(pc), .b(11'h1), .out(adder_2_out));  // open: cin, cout
  or or_1 (or_1_out, ret, rcall, acall);
  Multiplexer #(.width(8)) multiplexer_1 (
    .in0(subtractor_1_out), .in1(adder_1_out), .out(multiplexer_1_out), .sel(ret));
  Register sp (.D(multiplexer_1_out), .en(or_1_out), .clk(clk), .Q(sp_q), .clr(reset));
  Register #(.width(11)) register_1 (.D(multiplexer_2_out), .en(or_1_out), .clk(clk), .Q(ra), .clr(reset));
  Multiplexer #(.width(11)) multiplexer_2 (.in0(adder_2_out), .in1(ram_1_dout), .out(multiplexer_2_out), .sel(ret));
  RAM #(.dataWidth(11)) ram_1 (.addr(sp_q), .we(1'b1), .oe(1'b1), .clk(clk), .din(ra), .dout(ram_1_dout));
endmodule
