// Logisim project adders.circ as structural Verilog: 7 circuits, main circuit main
module main (
);

  \xor  xor_1 ();  // open: in1, in2, out
endmodule

module \xor  (
  input  in1,
  input  in2,
  output out
);

  wire and_1_out, and_2_out, not_1_out, not_2_out;

  not not_1 (not_1_out, in1);
  not not_2 (not_2_out, in2);
  and and_1 (and_1_out, not_1_out, in2);
  and and_2 (and_2_out, in1, not_2_out);
  or or_1 (out, and_1_out, and_2_out);
endmodule

module half_adder (
  input  in1,
  input  in2,
  output carry_bit,
  output sum
);

  and and_1 (carry_bit, in1, in2);
  \xor  xor_1 (.in1(in1), .in2(in2), .out(sum));
endmodule

module full_adder (
  input  in1,
  input  in2,
  input  carry_in,
  output carry_out,
  output sum
);

  wire half_adder_1_carry_bit, half_adder_1_sum, half_adder_2_carry_bit;

  half_adder half_adder_1 (.in1(in1), .in2(in2), .carry_bit(half_adder_1_carry_bit), .sum(half_adder_1_sum));
  half_adder half_adder_2 (.in1(half_adder_1_sum), .in2(carry_in), .carry_bit(half_adder_2_carry_bit), .sum(sum));
  or or_1 (carry_out, half_adder_1_carry_bit, half_adder_2_carry_bit);
endmodule

module two_bit_adder (
  input  a2,
  input  a1,
  input  b2,
  input  b1,
  input  carry_in,
  output carry_out,
  output sum2,
  output sum1
);

  wire full_adder_2_carry_out;

  full_adder full_adder_1 (.in1(a2), .in2(b2), .carry_in(full_adder_2_carry_out), .carry_out(carry_out), .sum(sum2));
  full_adder full_adder_2 (.in1(a1), .in2(b1), .carry_in(carry_in), .carry_out(full_adder_2_carry_out), .sum(sum1));
endmodule

module four_bit_adder (
  input  a4,
  input  a3,
  input  a2,
  input  a1,
  input  b4,
  input  b3,
  input  b2,
  input  b1,
  input  carry_in,
  output carry_out,
  output sum4,
  output sum3,
  output sum2,
  output sum1
);

  wire two_bit_adder_2_carry_out;

  two_bit_adder two_bit_adder_1 (
    .a2(a4), .a1(a3), .b2(b4), .b1(b3), .carry_in(two_bit_adder_2_carry_out), .carry_out(carry_out),
    .sum2(sum4), .sum1(sum3));
  two_bit_adder two_bit_adder_2 (
    .a2(a2), .a1(a1), .b2(b2), .b1(b1), .carry_in(carry_in), .carry_out(two_bit_adder_2_carry_out),
    .sum2(sum2), .sum1(sum1));
endmodule

module eight_bit_adder_no_carry (
  input  a8,
  input  a7,
  input  a6,
  input  a5,
  input  a4,
  input  a3,
  input  a2,
  input  a1,
  input  b8,
  input  b7,
  input  b6,
  input  b5,
  input  b4,
  input  b3,
  input  b2,
  input  b1,
  output out_17,
  output out_18,
  output out_19,
  output out_20,
  output out_21,
  output out_22,
  output out_23,
  output out_24
);

  wire four_bit_adder_1_carry_out;

  four_bit_adder four_bit_adder_1 (
    .a4(a4), .a3(a3), .a2(a2), .a1(a1), .b4(b4), .b3(b3), .b2(b2), .b1(b1),
    .carry_out(four_bit_adder_1_carry_out), .sum4(out_21), .sum3(out_22), .sum2(out_23), .sum1(out_24));  // open: carry_in
  four_bit_adder four_bit_adder_2 (
    .a4(a8), .a3(a7), .a2(a6), .a1(a5), .b4(b8), .b3(b7), .b2(b6), .b1(b5),
    .carry_in(four_bit_adder_1_carry_out), .sum4(out_17), .sum3(out_18), .sum2(out_19), .sum1(out_20));  // open: carry_out
endmodule
