// Logisim project alu_design.circ as structural Verilog: 4 circuits, main circuit ALU_main_8b
module ALU_main_8b (
  input  [4:0] opcode,
  input  [7:0] a,
  input  [7:0] b,
  input  cin,
  output [7:0] sum,
  output zero,
  output cout,
  output negative,
  output overflow
);

  wire add_sub_main_1_cout, and_1_out, nand_2_out;
  wire [7:0] add_sub_main_1_sum, and_2_out, multiplexer_1_out, multiplexer_2_out, multiplexer_3_out,
       multiplexer_4_out, multiplexer_5_out, nand_1_out, negator_1_out, nor_1_out, not_1_out, or_1_out,
       shifter_1_out, shifter_2_out, shifter_3_out, shifter_4_out, shifter_5_out, xnor_1_out, xor_1_out;
  wire [8:0] shifter_6_out, shifter_7_out;

  and and_1 (and_1_out, opcode[0], cin);
  Multiplexer #(.width(8)) multiplexer_1 (.in0(b), .in1(8'h1), .out(multiplexer_1_out), .sel(opcode[1]));
  Negator negator_1 (.in(a), .out(negator_1_out));
  Multiplexer #(.width(8)) multiplexer_2 (.in0(a), .in1(negator_1_out), .out(multiplexer_2_out), .sel(opcode[2]));
  add_sub_main add_sub_main_1 (
    .sub(opcode[2]), .cin(and_1_out), .a(a), .b(multiplexer_1_out), .sum(add_sub_main_1_sum),
    .cout(add_sub_main_1_cout), .overflow(overflow));
  assign not_1_out = ~a;  // NOT_Gate not_1, 8 bits wide
  assign and_2_out = a & b;  // AND_Gate and_2, 8 bits wide
  assign or_1_out = a | b;  // OR_Gate or_1, 8 bits wide
  assign xor_1_out = a ^ b;  // XOR_Gate xor_1, 8 bits wide
  assign nand_1_out = ~(a & b);  // NAND_Gate nand_1, 8 bits wide
  assign nor_1_out = ~(a | b);  // NOR_Gate nor_1, 8 bits wide
  assign xnor_1_out = ~(a ^ b);  // XNOR_Gate xnor_1, 8 bits wide
  Shifter shifter_1 (.in(a), .\dist (b[2:0]), .out(shifter_1_out));
  Shifter #(.shift("lr")) shifter_2 (.in(a), .\dist (b[2:0]), .out(shifter_2_out));
  Shifter #(.shift("ar")) shifter_3 (.in(a), .\dist (b[2:0]), .out(shifter_3_out));
  Shifter #(.shift("rl")) shifter_4 (.in(a), .\dist (b[2:0]), .out(shifter_4_out));
  Shifter #(.shift("rr")) shifter_5 (.in(a), .\dist (b[2:0]), .out(shifter_5_out));
  Shifter #(.shift("rl"), .width(9)) shifter_6 (.in({cin, a}), .\dist (b[3:0]), .out(shifter_6_out));
  Shifter #(.shift("rr"), .width(9)) shifter_7 (.in({cin, a}), .\dist (b[3:0]), .out(shifter_7_out));
  nand nand_2 (nand_2_out, opcode[0], opcode[1]);
  Multiplexer #(.width(8)) multiplexer_3 (
    .in0(multiplexer_2_out), .in1(add_sub_main_1_sum), .out(multiplexer_3_out), .sel(nand_2_out));
  Multiplexer #(.select(3), .width(8)) multiplexer_4 (
    .in0(not_1_out), .in1(and_2_out), .in2(or_1_out), .in3(xor_1_out), .in4(nand_1_out), .in5(nor_1_out),
    .in6(xnor_1_out), .in7({8{1'b0}}), .out(multiplexer_4_out), .sel(opcode[2:0]));
  Multiplexer #(.select(3), .width(8)) multiplexer_5 (
    .in0(shifter_1_out), .in1(shifter_2_out), .in2(shifter_3_out), .in3(shifter_4_out), .in4(shifter_5_out),
    .in5(shifter_6_out[7:0]), .in6(shifter_7_out[7:0]), .in7({8{1'b0}}), .out(multiplexer_5_out),
    .sel(opcode[2:0]));
  Multiplexer #(.select(2), .width(8)) multiplexer_6 (
    .in0(multiplexer_3_out), .in1(multiplexer_4_out), .in2(multiplexer_5_out), .in3({8{1'b0}}),
    .out({negative, sum[6:0]}), .sel(opcode[4:3]));
  Multiplexer #(.select(2)) multiplexer_7 (
    .in0(add_sub_main_1_cout), .in1(shifter_6_out[8]), .in2(shifter_7_out[8]), .in3(1'b0), .out(cout),
    .sel({opcode[4], opcode[1]}));
  zero_detect zero_detect_1 (.in_1({negative, sum[6:0]}), .out_2(zero));

  assign sum[7] = negative;
endmodule

module add_sub_main (
  input  sub,
  input  cin,
  input  [7:0] a,
  input  [7:0] b,
  output [7:0] sum,
  output cout,
  output overflow
);

  wire adder_1_cout, adder_2_cout, xor_2_out;
  wire [6:0] xor_1_out;
  wire [7:0] bit_extender_1_out;
  wire [7:7] xor_1_out_2;

  assign bit_extender_1_out = {{7{sub}}, sub};  // Bit_Extender bit_extender_1
  assign {xor_1_out_2[7], xor_1_out} = b ^ bit_extender_1_out;  // XOR_Gate xor_1, 8 bits wide
  xor xor_2 (xor_2_out, sub, cin);
  Adder #(.width(7)) adder_1 (.a(a[6:0]), .b(xor_1_out), .cin(xor_2_out), .cout(adder_1_cout));  // open: out
  Adder adder_2 (.a(a), .b({xor_1_out_2[7], xor_1_out}), .out(sum), .cin(xor_2_out), .cout(adder_2_cout));
  xor xor_3 (cout, adder_2_cout, sub);
  xor xor_4 (overflow, adder_2_cout, adder_1_cout);
endmodule

module ALU_4b (
  input  [3:0] opcode,
  input  cin,
  input  [3:0] a,
  input  [3:0] b,
  output [3:0] sum,
  output cout,
  output zero,
  output negative,
  output overflow
);

  wire adder_1_cout, adder_2_cout, adder_4_cout, adder_5_cout, multiplexer_3_out, subtractor_1_bout,
       subtractor_2_bout, subtractor_4_bout, subtractor_5_bout;
  wire [3:0] adder_1_out, adder_2_out, adder_3_out, and_1_out, negator_1_out, not_1_out, or_1_out,
       shifter_1_out, shifter_2_out, shifter_3_out, shifter_4_out, shifter_5_out, subtractor_1_out,
       subtractor_2_out, subtractor_3_out, xor_1_out;

  Adder #(.width(4)) adder_1 (.a(a), .b(b), .out(adder_1_out), .cout(adder_1_cout));  // open: cin
  Adder #(.width(4)) adder_2 (.a(a), .b(b), .out(adder_2_out), .cin(cin), .cout(adder_2_cout));
  Subtractor #(.width(4)) subtractor_1 (.a(a), .b(b), .out(subtractor_1_out), .bout(subtractor_1_bout));  // open: bin
  Subtractor #(.width(4)) subtractor_2 (.a(a), .b(b), .out(subtractor_2_out), .bin(cin), .bout(subtractor_2_bout));
  Negator #(.width(4)) negator_1 (.in(a), .out(negator_1_out));
  Adder #(.width(4)) adder_3 (.a(a), .b(4'b0001), .out(adder_3_out));  // open: cin, cout
  Subtractor #(.width(4)) subtractor_3 (.a(a), .b(4'b0001), .out(subtractor_3_out));  // open: bin, bout
  assign and_1_out = a & b;  // AND_Gate and_1, 4 bits wide
  assign or_1_out = a | b;  // OR_Gate or_1, 4 bits wide
  assign xor_1_out = a ^ b;  // XOR_Gate xor_1, 4 bits wide
  assign not_1_out = ~a;  // NOT_Gate not_1, 4 bits wide
  Shifter #(.width(4)) shifter_1 (.in(a), .\dist (b[1:0]), .out(shifter_1_out));
  Shifter #(.shift("lr"), .width(4)) shifter_2 (.in(a), .\dist (b[1:0]), .out(shifter_2_out));
  Shifter #(.shift("ar"), .width(4)) shifter_3 (.in(a), .\dist (b[1:0]), .out(shifter_3_out));
  Shifter #(.shift("rl"), .width(4)) shifter_4 (.in(a), .\dist (b[1:0]), .out(shifter_4_out));
  Shifter #(.shift("rr"), .width(4)) shifter_5 (.in(a), .\dist (b[1:0]), .out(shifter_5_out));
  Adder #(.width(3)) adder_4 (.a(a[2:0]), .b(b[2:0]), .cout(adder_4_cout));  // open: out, cin
  Adder #(.width(3)) adder_5 (.a(a[2:0]), .b(b[2:0]), .cin(cin), .cout(adder_5_cout));  // open: out
  Subtractor #(.width(3)) subtractor_4 (.a(a[2:0]), .b(b[2:0]), .bout(subtractor_4_bout));  // open: out, bin
  Subtractor #(.width(3)) subtractor_5 (.a(a[2:0]), .b(b[2:0]), .bin(cin), .bout(subtractor_5_bout));  // open: out
  Multiplexer #(.select(4), .width(4)) multiplexer_1 (
    .in0(adder_1_out), .in1(adder_2_out), .in2(subtractor_1_out), .in3(subtractor_2_out),
    .in4(negator_1_out), .in5(adder_3_out), .in6(subtractor_3_out), .in7(and_1_out), .in8(or_1_out),
    .in9(xor_1_out), .in10(not_1_out), .in11(shifter_1_out), .in12(shifter_2_out), .in13(shifter_3_out),
    .in14(shifter_4_out), .in15(shifter_5_out), .out(sum), .sel(opcode));
  Multiplexer #(.select(4)) multiplexer_2 (
    .in0(adder_1_cout), .in1(adder_2_cout), .in2(subtractor_1_bout), .in3(subtractor_2_bout), .in4(1'b0),
    .in5(1'b0), .in6(1'b0), .in7(1'b0), .in8(1'b0), .in9(1'b0), .in10(1'b0), .in11(1'b0), .in12(1'b0),
    .in13(1'b0), .in14(1'b0), .in15(1'b0), .out(cout), .sel(opcode));
  Multiplexer #(.select(4)) multiplexer_3 (
    .in0(adder_4_cout), .in1(adder_5_cout), .in2(subtractor_4_bout), .in3(subtractor_5_bout), .in4(1'b0),
    .in5(1'b0), .in6(1'b0), .in7(1'b0), .in8(1'b0), .in9(1'b0), .in10(1'b0), .in11(1'b0), .in12(1'b0),
    .in13(1'b0), .in14(1'b0), .in15(1'b0), .out(multiplexer_3_out), .sel(opcode));
  nor nor_1 (zero, sum[0], sum[1], sum[2], sum[3]);
  BitSelector #(.width(4)) bitselector_1 (.in(sum), .out(negative), .sel(2'b11));
  xor xor_2 (overflow, cout, multiplexer_3_out);
endmodule

module zero_detect (
  input  [7:0] in_1,
  output out_2
);

  nand nand_1 (out_2, in_1[0], in_1[1], in_1[2], in_1[3], in_1[4], in_1[5], in_1[6], in_1[7]);
endmodule
