// Logisim project Foundations.circ as structural Verilog
module full_adder (
  input  a,
  input  b,
  input  cin,
  output cout,
  output sum
);

  wire and_1_out, and_2_out, xor_1_out;

  and and_1 (and_1_out, a, b);
  xor xor_1 (xor_1_out, a, b);
  and and_2 (and_2_out, xor_1_out, cin);
  xor xor_2 (sum, xor_1_out, cin);
  or or_1 (cout, and_1_out, and_2_out);
endmodule

module four_bit_adder (
  input  a4,
  input  a3,
  input  a2,
  input  a1,
  input  b4,
  input  b3,
  input  b2,
  input  b1,
  input  carry_in,
  output carry_out,
  output s4,
  output s3,
  output s2,
  output s1
);

  wire full_adder_2_cout, full_adder_3_cout, full_adder_4_cout;

  full_adder full_adder_1 (.a(a4), .b(b4), .cin(full_adder_2_cout), .cout(carry_out), .sum(s4));
  full_adder full_adder_2 (.a(a3), .b(b3), .cin(full_adder_3_cout), .cout(full_adder_2_cout), .sum(s3));
  full_adder full_adder_3 (.a(a2), .b(b2), .cin(full_adder_4_cout), .cout(full_adder_3_cout), .sum(s2));
  full_adder full_adder_4 (.a(a1), .b(b1), .cin(carry_in), .cout(full_adder_4_cout), .sum(s1));
endmodule

module four_bit_subtractor (
  input  a4,
  input  a3,
  input  a2,
  input  a1,
  input  b4,
  input  b3,
  input  b2,
  input  b1,
  output cout,
  output out4,
  output out3,
  output out2,
  output out1
);

  wire bitwise_not_1_out1, bitwise_not_1_out2, bitwise_not_1_out3, bitwise_not_1_out4;

  bitwise_not bitwise_not_1 (
    .in4(b4), .in3(b3), .in2(b2), .in1(b1), .out4(bitwise_not_1_out4), .out3(bitwise_not_1_out3),
    .out2(bitwise_not_1_out2), .out1(bitwise_not_1_out1));
  four_bit_adder four_bit_adder_1 (
    .a4(a4), .a3(a3), .a2(a2), .a1(a1), .b4(bitwise_not_1_out4), .b3(bitwise_not_1_out3),
    .b2(bitwise_not_1_out2), .b1(bitwise_not_1_out1), .carry_in(1'b1), .carry_out(cout), .s4(out4),
    .s3(out3), .s2(out2), .s1(out1));
endmodule

module adder_subtractor (
  input  a4,
  input  a3,
  input  a2,
  input  a1,
  input  b4,
  input  b3,
  input  b2,
  input  b1,
  input  carry_in,
  output overflow_flag,
  output out4,
  output out3,
  output out2,
  output out1
);

  wire bitwise_xor_1_out1, bitwise_xor_1_out2, bitwise_xor_1_out3, bitwise_xor_1_out4;

  bitwise_xor bitwise_xor_1 (
    .a4(b4), .a3(b3), .a2(b2), .a1(b1), .b4(carry_in), .b3(carry_in), .b2(carry_in), .b1(carry_in),
    .out4(bitwise_xor_1_out4), .out3(bitwise_xor_1_out3), .out2(bitwise_xor_1_out2), .out1(bitwise_xor_1_out1));
  four_bit_adder four_bit_adder_1 (
    .a4(a4), .a3(a3), .a2(a2), .a1(a1), .b4(bitwise_xor_1_out4), .b3(bitwise_xor_1_out3),
    .b2(bitwise_xor_1_out2), .b1(bitwise_xor_1_out1), .carry_in(carry_in), .carry_out(overflow_flag),
    .s4(out4), .s3(out3), .s2(out2), .s1(out1));
endmodule

module bitwise_not (
  input  in4,
  input  in3,
  input  in2,
  input  in1,
  output out4,
  output out3,
  output out2,
  output out1
);

  not not_1 (out4, in4);
  not not_2 (out3, in3);
  not not_3 (out2, in2);
  not not_4 (out1, in1);
endmodule

module bitwise_and (
  input  a4,
  input  a3,
  input  a2,
  input  a1,
  input  b4,
  input  b3,
  input  b2,
  input  b1,
  output out4,
  output out3,
  output out2,
  output out1
);

  and and_1 (out4, a4, b4);
  and and_2 (out3, a3, b3);
  and and_3 (out2, a2, b2);
  and and_4 (out1, a1, b1);
endmodule

module bitwise_or (
  input  a4,
  input  a3,
  input  a2,
  input  a1,
  input  b4,
  input  b3,
  input  b2,
  input  b1,
  output out4,
  output out3,
  output out2,
  output out1
);

  or or_1 (out4, a4, b4);
  or or_2 (out3, a3, b3);
  or or_3 (out2, a2, b2);
  or or_4 (out1, a1, b1);
endmodule

module bitwise_xor (
  input  a4,
  input  a3,
  input  a2,
  input  a1,
  input  b4,
  input  b3,
  input  b2,
  input  b1,
  output out4,
  output out3,
  output out2,
  output out1
);

  xor xor_1 (out4, a4, b4);
  xor xor_2 (out3, a3, b3);
  xor xor_3 (out2, a2, b2);
  xor xor_4 (out1, a1, b1);
endmodule

module zero_detector (
  input  in4,
  input  in3,
  input  in2,
  input  in1,
  output out_5
);

  wire or_1_out, or_2_out, or_3_out;

  or or_1 (or_1_out, in4, in3);
  or or_2 (or_2_out, in2, in1);
  or or_3 (or_3_out, or_1_out, or_2_out);
  not not_1 (out_5, or_3_out);
endmodule

module shift_right (
  input  in4,
  input  in3,
  input  in2,
  input  in1,
  output out4,
  output out3,
  output out2,
  output out1
);


  assign out1 = in2;
  assign out2 = in3;
  assign out3 = in4;
  assign out4 = 1'b0;
endmodule

module logical_shift_left (
  input  in4,
  input  in3,
  input  in2,
  input  in1,
  output out4,
  output out3,
  output out2,
  output out1
);


  assign out1 = 1'b0;
  assign out2 = in1;
  assign out3 = in2;
  assign out4 = in3;
endmodule

module arithmetic_shift_left (
  input  in4,
  input  in3,
  input  in2,
  input  in1,
  output out4,
  output out3,
  output out2,
  output out1
);


  assign out1 = 1'b0;
  assign out2 = in1;
  assign out3 = in2;
  assign out4 = in4;
endmodule

module multiplexer_2_1 (
  input  a,
  input  b,
  input  selector,
  output val_out
);

  wire and_1_out, and_2_out, not_1_out;

  and and_1 (and_1_out, selector, a);
  not not_1 (not_1_out, selector);
  and and_2 (and_2_out, not_1_out, b);
  or or_1 (val_out, and_1_out, and_2_out);
endmodule

module multiplexer_4_1 (
  input  a,
  input  b,
  input  c,
  input  d,
  input  s1,
  input  s2,
  output val_out
);

  wire multiplexer_2_1_1_val_out, multiplexer_2_1_2_val_out;

  multiplexer_2_1 multiplexer_2_1_1 (.a(a), .b(b), .selector(s1), .val_out(multiplexer_2_1_1_val_out));
  multiplexer_2_1 multiplexer_2_1_2 (.a(c), .b(d), .selector(s1), .val_out(multiplexer_2_1_2_val_out));
  multiplexer_2_1 multiplexer_2_1_3 (
    .a(multiplexer_2_1_1_val_out), .b(multiplexer_2_1_2_val_out), .selector(s2), .val_out(val_out));
endmodule

module multiplexer_16_1 (
  input  in1,
  input  in2,
  input  in3,
  input  in4,
  input  in5,
  input  in6,
  input  in7,
  input  in8,
  input  s1,
  input  s2,
  output val_out
);

  wire undriven, undriven_2;

  multiplexer_4_1 multiplexer_4_1_1 (.a(in1), .b(in2), .c(in3), .d(in4), .s1(s1), .s2(s2));  // open: val_out
  multiplexer_4_1 multiplexer_4_1_2 (.a(in5), .b(in6), .c(in7), .d(in8), .s1(s1), .s2(s2));  // open: val_out
  multiplexer_2_1 multiplexer_2_1_1 (.a(undriven), .b(undriven_2), .val_out(val_out));  // open: selector
endmodule

module rotate_left (
  input  in4,
  input  in3,
  input  in2,
  input  in1,
  output out4,
  output out3,
  output out2,
  output out1
);


  assign out1 = in4;
  assign out2 = in1;
  assign out3 = in2;
  assign out4 = in3;
endmodule

module rotate_right (
  input  in4,
  input  in3,
  input  in2,
  input  in1,
  output out4,
  output out3,
  output out2,
  output out1
);


  assign out1 = in2;
  assign out2 = in3;
  assign out3 = in4;
  assign out4 = in1;
endmodule

module rotate_carry_left (
  input  in4,
  input  in3,
  input  in2,
  input  in1,
  input  cin,
  output out4,
  output out3,
  output out2,
  output out1,
  output cout
);


  assign cout = in4;
  assign out1 = cin;
  assign out2 = in1;
  assign out3 = in2;
  assign out4 = in3;
endmodule

module rotate_carry_right (
  input  in4,
  input  in3,
  input  in2,
  input  in1,
  input  cin,
  output out4,
  output out3,
  output out2,
  output out1,
  output cout
);


  assign cout = in1;
  assign out1 = in2;
  assign out2 = in3;
  assign out3 = in4;
  assign out4 = cin;
endmodule
