// Logisim project register_design.circ as structural Verilog
module register_file_8 (
  input  [7:0] write_data,
  input  [2:0] write_address,
  input  write_enable,
  input  [2:0] read_address_A,
  input  clock,
  input  reset,
  input  [2:0] read_address_B,
  input  [3:0] in_8,
  output [7:0] read_data_A,
  output [7:0] read_data_B
);

  wire buffer_2_out, decoder_1_out1, decoder_1_out2, decoder_1_out3, decoder_1_out4, decoder_1_out5,
       decoder_1_out6, decoder_1_out7;
  wire [7:0] buffer_1_out, register_2_q, register_3_q, register_4_q, register_5_q, register_6_q, register_8_q;

  Register register_1 (.en(in_8[0]));  // open: D, clk, Q, clr
  assign buffer_1_out = write_data;  // Buffer buffer_1, 8 bits wide
  Decoder #(.select(3)) decoder_1 (
    .out1(decoder_1_out1), .out2(decoder_1_out2), .out3(decoder_1_out3), .out4(decoder_1_out4),
    .out5(decoder_1_out5), .out6(decoder_1_out6), .out7(decoder_1_out7), .sel(write_address),
    .en(write_enable));  // open: out0
  buf buffer_2 (buffer_2_out, clock);
  Register register_2 (.D(buffer_1_out), .en(decoder_1_out1), .clk(buffer_2_out), .Q(register_2_q), .clr(reset));
  Register register_3 (.D(buffer_1_out), .en(decoder_1_out2), .clk(buffer_2_out), .Q(register_3_q), .clr(reset));
  Register register_4 (.D(buffer_1_out), .en(decoder_1_out3), .clk(buffer_2_out), .Q(register_4_q), .clr(reset));
  Register register_5 (.D(buffer_1_out), .en(decoder_1_out4), .clk(buffer_2_out), .Q(register_5_q), .clr(reset));
  Register register_6 (.D(buffer_1_out), .en(decoder_1_out5), .clk(buffer_2_out), .Q(register_6_q), .clr(reset));
  Register register_7 (.D(buffer_1_out), .en(decoder_1_out6), .clk(buffer_2_out), .Q(register_6_q), .clr(reset));
  Register register_8 (.D(buffer_1_out), .en(decoder_1_out7), .clk(buffer_2_out), .Q(register_8_q), .clr(reset));
  Multiplexer #(.select(3), .width(8)) multiplexer_1 (
    .in0({8{1'b0}}), .in1(register_2_q), .in2(register_3_q), .in3(register_4_q), .in4(register_5_q),
    .in5(register_6_q), .in6(register_6_q), .in7(register_8_q), .out(read_data_A), .sel(read_address_A));
  Multiplexer #(.select(3), .width(8)) multiplexer_2 (
    .in0({8{1'b0}}), .in1(register_2_q), .in2(register_3_q), .in3(register_4_q), .in4(register_5_q),
    .in5(register_6_q), .in6(register_6_q), .in7(register_8_q), .out(read_data_B), .sel(read_address_B));
  // Pins of 1 and 4 bits meet at in_8
endmodule

module sr_latch (
  input  in_1,
  input  in_2,
  output out_3,
  output out_4
);

  nor nor_1 (out_3, in_1, out_4);
  nor nor_2 (out_4, out_3, in_2);
endmodule

module gated_sr_latch (
  input  in_1,
  input  in_2,
  input  in_3,
  output out_4,
  output out_5
);

  wire and_1_out, and_2_out;

  and and_1 (and_1_out, in_1, in_2);
  and and_2 (and_2_out, in_2, in_3);
  nor nor_1 (out_4, and_1_out, out_5);
  nor nor_2 (out_5, out_4, and_2_out);
endmodule

module gated_d_latch (
  input  in_1,
  input  in_2,
  output out_3,
  output out_4
);

  wire and_1_out, and_2_out, not_1_out;

  not not_1 (not_1_out, in_1);
  and and_1 (and_1_out, not_1_out, in_2);
  and and_2 (and_2_out, in_2, in_1);
  nor nor_1 (out_3, and_1_out, out_4);
  nor nor_2 (out_4, out_3, and_2_out);
endmodule

module nand_gated_sr (
  input  in_1,
  input  in_2,
  input  in_3,
  output out_4,
  output out_5
);

  wire nand_1_out, nand_2_out;

  nand nand_1 (nand_1_out, in_1, in_2);
  nand nand_2 (nand_2_out, in_2, in_3);
  nand nand_3 (out_4, nand_1_out, out_5);
  nand nand_4 (out_5, out_4, nand_2_out);
endmodule

module nand_gated_d (
  input  in_1,
  input  in_2,
  output out_3,
  output out_4
);

  wire nand_1_out, nand_2_out, not_1_out;

  not not_1 (not_1_out, in_1);
  nand nand_1 (nand_1_out, in_1, in_2);
  nand nand_2 (nand_2_out, in_2, not_1_out);
  nand nand_3 (out_3, nand_1_out, out_4);
  nand nand_4 (out_4, out_3, nand_2_out);
endmodule

module master_slave_dff (
  input  in_1,
  output out_2,
  output out_3
);

  wire clock_1_out, gated_d_latch_1_out_3, not_1_out;

  Clock clock_1 (.out(clock_1_out));
  gated_d_latch gated_d_latch_1 (.in_2(clock_1_out), .in_1(in_1), .out_3(gated_d_latch_1_out_3));  // open: out_4
  not not_1 (not_1_out, clock_1_out);
  gated_d_latch gated_d_latch_2 (.in_2(not_1_out), .in_1(gated_d_latch_1_out_3), .out_3(out_2), .out_4(out_3));
endmodule

module pos_edge_dff (
  input  data,
  output out_2,
  output out_3
);

  wire clock_1_out, nand_1_out, nand_2_out, nand_3_out, nand_4_out;

  Clock clock_1 (.out(clock_1_out));
  nand nand_1 (nand_1_out, nand_4_out, nand_2_out);
  nand nand_2 (nand_2_out, nand_1_out, clock_1_out);
  nand nand_3 (nand_3_out, nand_2_out, clock_1_out, nand_4_out);
  nand nand_4 (nand_4_out, nand_3_out, data);
  nand nand_5 (out_2, nand_2_out, out_3);
  nand nand_6 (out_3, out_2, nand_3_out);
endmodule

module register_8b (
  input  [7:0] in8,
  input  clk,
  output [7:0] out8
);

  D_Flip_Flop d_ff_1 (.D(in8[7]), .clk(clk), .Q(out8[7]));  // open: Qn, preset, reset
  D_Flip_Flop d_ff_2 (.D(in8[6]), .clk(clk), .Q(out8[6]));  // open: Qn, preset, reset
  D_Flip_Flop d_ff_3 (.D(in8[5]), .clk(clk), .Q(out8[5]));  // open: Qn, preset, reset
  D_Flip_Flop d_ff_4 (.D(in8[4]), .clk(clk), .Q(out8[4]));  // open: Qn, preset, reset
  D_Flip_Flop d_ff_5 (.D(in8[3]), .clk(clk), .Q(out8[3]));  // open: Qn, preset, reset
  D_Flip_Flop d_ff_6 (.D(in8[2]), .clk(clk), .Q(out8[2]));  // open: Qn, preset, reset
  D_Flip_Flop d_ff_7 (.D(in8[1]), .clk(clk), .Q(out8[1]));  // open: Qn, preset, reset
  D_Flip_Flop d_ff_8 (.D(in8[0]), .clk(clk), .Q(out8[0]));  // open: Qn, preset, reset
endmodule
